# Fritzing sketch perkit_control (saved by Fritzing 0.3.6b)
breadboards: 1

parts:
  Arduino1 = Arduino
  S1 = Pushbutton [package=THT]
  LED1 = Red LED - 5mm
  R2 = 10 Ω Resistor [package=THT]
  R2_2 = 10 Ω Resistor [package=THT]
  S1_2 = Pushbutton [package=THT]
  LED1_2 = Red LED - 5mm
  R3 = Rotary Potentiometer (Large) [package=THT]
  C5 = Ceramic Capacitor [package=THT]

nets:
  N1: Arduino1.GND, LED1.cathode
  N2: Arduino1.D2, S1.Pin_1, S1.Pin_2, LED1.anode
  N3: Arduino1.+5V, R2.Pin_0
  N4: S1.Pin_3, S1.Pin_4, R2.Pin_1
  N5: R2_2.Pin_0, S1_2.Pin_3, S1_2.Pin_4
  N6: S1_2.Pin_1, S1_2.Pin_2, LED1_2.anode
  N7: LED1_2.cathode, R3.leg2, C5.pin_1
  N8: R3.leg1, C5.pin_0

notes:
  The switch represents a one step Dial switch.
  This is the Skip switch - a push to make switch.
